# Fritzing sketch circalamp (saved by Fritzing 0.9.3b)
perfboards: 1
breadboards: 1

parts:
  Part3 = Arduino Uno (Rev3)
  U5 = ESP8266 WiFi Module [part_number=ESP8266]  # not connected
  R10 = Resistor [tolerance=±5% resistance=10k package=THT]
  ZS-042_RTC2 = ZS-042 RTC Module
  S1 = Pushbutton [package="[THT]"]
  R11 = Resistor [tolerance=±5% resistance=10k package=THT]

nets:
  N1: Part3.A4/SDA, ZS-042_RTC2.SDA
  N2: Part3.A5/SCL, ZS-042_RTC2.SCL
  N3: Part3.GND, S1.Pin_1, S1.Pin_2
  N4: Part3.3V3, R10.Pin_0, R11.Pin_0
  5V: Part3.5V, ZS-042_RTC2.VCC
  N5: S1.Pin_3, S1.Pin_4, R11.Pin_1

custom parts:
  ESP8266 WiFi Module: Generic WiFi Module based on the ESP8266 with onboard PCB antenna and UART communications
